// Logisim project p3.circ as structural Verilog: 7 circuits, main circuit main
module main (
  input  Reset,
  output [31:0] out_2,
  output out_3,
  output [4:0] out_4,
  output [31:0] out_5,
  output out_6,
  output [4:0] out_7,
  output [31:0] out_8
);

  wire alu_1_zero, ALUSrc, and_1_out, Branch, clk, ExtOp, MemroReg, RegDst;
  wire [2:0] ALUOp;
  wire [4:0] inssplitter_1_rd, inssplitter_1_rs, inssplitter_1_rt, s;
  wire [5:0] inssplitter_1_funct, inssplitter_1_op;
  wire [15:0] inssplitter_1_imme;
  wire [31:0] alu_1_aluresult, ext_1_out, grf_1_rd1, multiplexer_2_out, ram_1_data, shifter_1_out,
       shifter_2_out;

  Clock Clock (.out(clk));
  controller controller_1 (
    .OP(inssplitter_1_op), .Funct(inssplitter_1_funct), .MemtoReg(MemroReg), .MemWrite(out_6),
    .Branch(Branch), .ALUop_2_0(ALUOp), .ALUSrc(ALUSrc), .RegDst(RegDst), .RegWrite(out_3), .ExtOp(ExtOp));
  ifu ifu_1 (.branch(and_1_out), .branchAddr(shifter_1_out), .clk(clk), .rst(Reset), .OpCode(out_2));
  InsSplitter inssplitter_1 (
    .instructure(out_2), .Op(inssplitter_1_op), .Funct(inssplitter_1_funct), .rs(inssplitter_1_rs),
    .rt(inssplitter_1_rt), .rd(inssplitter_1_rd), .s(s), .imme(inssplitter_1_imme));
  ext ext_1 (.In(inssplitter_1_imme), .ExtOp(ExtOp), .Out(ext_1_out));
  Multiplexer #(.width(5), .enable("false")) multiplexer_1 (
    .in0(inssplitter_1_rt), .in1(inssplitter_1_rd), .out(out_4), .sel(RegDst));
  grf grf_1 (
    .A1(inssplitter_1_rs), .A2(inssplitter_1_rt), .A3(out_4), .WD(out_5), .RD1(grf_1_rd1), .RD2(out_8),
    .clk(clk), .reset(Reset), .WE(out_3));
  Multiplexer #(.width(32), .enable("false")) multiplexer_2 (
    .in0(out_8), .in1(ext_1_out), .out(multiplexer_2_out), .sel(ALUSrc));
  Shifter #(.width(32)) shifter_1 (.in(ext_1_out), .\dist (5'b00010), .out(shifter_1_out));
  and and_1 (and_1_out, Branch, alu_1_zero);
  alu alu_1 (
    .SrcA(grf_1_rd1), .SrcB(multiplexer_2_out), .s(s), .ALUop(ALUOp), .Zero(alu_1_zero),
    .ALUResult(alu_1_aluresult));
  Bit_Extender #(.in_width(32), .out_width(5)) bit_extender_1 (.in(shifter_2_out), .out(out_7));
  Shifter #(.width(32), .shift("lr")) shifter_2 (.in(alu_1_aluresult), .\dist (5'b00010), .out(shifter_2_out));
  RAM #(.addrWidth(5), .dataWidth(32), .bus("separate")) ram_1 (
    .addr(out_7), .din(out_8), .data(ram_1_data), .str(out_6), .clk(clk), .clr(Reset));  // open: sel, ld
  Multiplexer #(.width(32), .enable("false")) multiplexer_3 (
    .in0(alu_1_aluresult), .in1(ram_1_data), .out(out_5), .sel(MemroReg));

  // Other names for the same wires on the sheet: Instr[31:0] = out_2; MemAddr[4:0] = out_7; MemData[31:0] = out_8;
  //   MemWrite = out_6; RegAddr[4:0] = out_4; RegData[31:0] = out_5; RegWrite = out_3; rst = Reset
endmodule

// GRF
module grf (
  input  WE,
  input  [4:0] A1,
  input  [4:0] A2,
  input  [4:0] A3,
  input  [31:0] WD,
  input  clk,
  input  reset,
  output [31:0] RD1,
  output [31:0] RD2
);

  wire I0, I1, I2, I3, I4, I5, I6, I7, I8, I9, I10, I11, I12, I13, I14, I15, I16, I17, I18, I19, I20, I21,
       I22, I23, I24, I25, I26, I27, I28, I29, I30, I31;
  wire [31:0] O1, O2, O3, O4, O5, O6, O7, O8, O9, O10, O11, O12, O13, O14, O15, O16, O17, O18, O19, O20, O21,
       O22, O23, O24, O25, O26, O27, O28, O29, O30, O31;

  Register #(.width(32)) register_1 (.D(WD), .en(I0), .clk(clk), .clr(reset));  // open: Q
  Register #(.width(32)) register_2 (.D(WD), .en(I4), .Q(O4), .clk(clk), .clr(reset));
  Register #(.width(32)) register_3 (.D(WD), .en(I8), .Q(O8), .clk(clk), .clr(reset));
  Register #(.width(32)) register_4 (.D(WD), .en(I12), .Q(O12), .clk(clk), .clr(reset));
  Register #(.width(32)) register_5 (.D(WD), .en(I16), .Q(O16), .clk(clk), .clr(reset));
  Register #(.width(32)) register_6 (.D(WD), .en(I20), .Q(O20), .clk(clk), .clr(reset));
  Register #(.width(32)) register_7 (.D(WD), .en(I24), .Q(O24), .clk(clk), .clr(reset));
  Register #(.width(32)) register_8 (.D(WD), .en(I28), .Q(O28), .clk(clk), .clr(reset));
  Register #(.width(32)) register_9 (.D(WD), .en(I1), .Q(O1), .clk(clk), .clr(reset));
  Register #(.width(32)) register_10 (.D(WD), .en(I5), .Q(O5), .clk(clk), .clr(reset));
  Register #(.width(32)) register_11 (.D(WD), .en(I9), .Q(O9), .clk(clk), .clr(reset));
  Register #(.width(32)) register_12 (.D(WD), .en(I13), .Q(O13), .clk(clk), .clr(reset));
  Register #(.width(32)) register_13 (.D(WD), .en(I17), .Q(O17), .clk(clk), .clr(reset));
  Register #(.width(32)) register_14 (.D(WD), .en(I21), .Q(O21), .clk(clk), .clr(reset));
  Register #(.width(32)) register_15 (.D(WD), .en(I25), .Q(O25), .clk(clk), .clr(reset));
  Register #(.width(32)) register_16 (.D(WD), .en(I29), .Q(O29), .clk(clk), .clr(reset));
  Decoder #(.select(5), .disabled(0)) decoder_1 (
    .out0(I0), .out1(I1), .out2(I2), .out3(I3), .out4(I4), .out5(I5), .out6(I6), .out7(I7), .out8(I8),
    .out9(I9), .out10(I10), .out11(I11), .out12(I12), .out13(I13), .out14(I14), .out15(I15), .out16(I16),
    .out17(I17), .out18(I18), .out19(I19), .out20(I20), .out21(I21), .out22(I22), .out23(I23), .out24(I24),
    .out25(I25), .out26(I26), .out27(I27), .out28(I28), .out29(I29), .out30(I30), .out31(I31), .sel(A3),
    .en(WE));
  Register #(.width(32)) register_17 (.D(WD), .en(I2), .Q(O2), .clk(clk), .clr(reset));
  Register #(.width(32)) register_18 (.D(WD), .en(I6), .Q(O6), .clk(clk), .clr(reset));
  Register #(.width(32)) register_19 (.D(WD), .en(I10), .Q(O10), .clk(clk), .clr(reset));
  Register #(.width(32)) register_20 (.D(WD), .en(I14), .Q(O14), .clk(clk), .clr(reset));
  Register #(.width(32)) register_21 (.D(WD), .en(I18), .Q(O18), .clk(clk), .clr(reset));
  Register #(.width(32)) register_22 (.D(WD), .en(I22), .Q(O22), .clk(clk), .clr(reset));
  Register #(.width(32)) register_23 (.D(WD), .en(I26), .Q(O26), .clk(clk), .clr(reset));
  Register #(.width(32)) register_24 (.D(WD), .en(I30), .Q(O30), .clk(clk), .clr(reset));
  Register #(.width(32)) register_25 (.D(WD), .en(I3), .Q(O3), .clk(clk), .clr(reset));
  Register #(.width(32)) register_26 (.D(WD), .en(I7), .Q(O7), .clk(clk), .clr(reset));
  Register #(.width(32)) register_27 (.D(WD), .en(I11), .Q(O11), .clk(clk), .clr(reset));
  Register #(.width(32)) register_28 (.D(WD), .en(I15), .Q(O15), .clk(clk), .clr(reset));
  Register #(.width(32)) register_29 (.D(WD), .en(I19), .Q(O19), .clk(clk), .clr(reset));
  Register #(.width(32)) register_30 (.D(WD), .en(I23), .Q(O23), .clk(clk), .clr(reset));
  Register #(.width(32)) register_31 (.D(WD), .en(I27), .Q(O27), .clk(clk), .clr(reset));
  Register #(.width(32)) register_32 (.D(WD), .en(I31), .Q(O31), .clk(clk), .clr(reset));
  Multiplexer #(.select(5), .width(32), .enable("false")) multiplexer_1 (
    .in0({32{1'b0}}), .in1(O1), .in2(O2), .in3(O3), .in4(O4), .in5(O5), .in6(O6), .in7(O7), .in8(O8),
    .in9(O9), .in10(O10), .in11(O11), .in12(O12), .in13(O13), .in14(O14), .in15(O15), .in16(O16), .in17(O17),
    .in18(O18), .in19(O19), .in20(O20), .in21(O21), .in22(O22), .in23(O23), .in24(O24), .in25(O25),
    .in26(O26), .in27(O27), .in28(O28), .in29(O29), .in30(O30), .in31(O31), .out(RD1), .sel(A1));
  Multiplexer #(.select(5), .width(32), .enable("false")) multiplexer_2 (
    .in0({32{1'b0}}), .in1(O1), .in2(O2), .in3(O3), .in4(O4), .in5(O5), .in6(O6), .in7(O7), .in8(O8),
    .in9(O9), .in10(O10), .in11(O11), .in12(O12), .in13(O13), .in14(O14), .in15(O15), .in16(O16), .in17(O17),
    .in18(O18), .in19(O19), .in20(O20), .in21(O21), .in22(O22), .in23(O23), .in24(O24), .in25(O25),
    .in26(O26), .in27(O27), .in28(O28), .in29(O29), .in30(O30), .in31(O31), .out(RD2), .sel(A2));
endmodule

// IFU
module ifu (
  input  branch,
  input  [31:0] branchAddr,
  input  clk,
  input  rst,
  output [31:0] OpCode
);

  wire [4:0] bit_extender_1_out;
  wire [31:0] adder_1_out, adder_2_out, multiplexer_1_out, PC_q, shifter_1_out;

  Adder #(.width(32)) adder_1 (.a(adder_2_out), .b(branchAddr), .out(adder_1_out));  // open: cin, cout
  Multiplexer #(.width(32), .enable("false")) multiplexer_1 (
    .in0(adder_2_out), .in1(adder_1_out), .out(multiplexer_1_out), .sel(branch));
  Register #(.width(32)) PC (.D(multiplexer_1_out), .Q(PC_q), .clk(clk), .clr(rst));  // open: en
  Adder #(.width(32)) adder_2 (.a(32'h4), .b(PC_q), .out(adder_2_out));  // open: cin, cout
  Shifter #(.width(32), .shift("lr")) shifter_1 (.in(PC_q), .\dist (5'b00010), .out(shifter_1_out));
  Bit_Extender #(.in_width(32), .out_width(5)) bit_extender_1 (.in(shifter_1_out), .out(bit_extender_1_out));
  ROM #(.addrWidth(5), .dataWidth(32)) rom_1 (.addr(bit_extender_1_out), .data(OpCode));  // open: sel

  // Notes on the sheet:
  //   contents of rom_1 (hex, n*v repeats v):
  //   340103ff 3c02007f 10880 21140 ac010000 ac020004 221821
endmodule

// ALU
module alu (
  input  [31:0] SrcA,
  input  [31:0] SrcB,
  input  [4:0] s,
  input  [2:0] ALUop,
  output Zero,
  output [31:0] ALUResult
);

  wire [31:0] adder_1_out, and_1_out, and_2_out, or_1_out, or_2_out, shifter_1_out, shifter_2_out,
       subtractor_1_out;

  assign and_1_out = SrcA & SrcB;  // AND_Gate and_1, 32 bits wide
  assign or_1_out = SrcA | SrcB;  // OR_Gate or_1, 32 bits wide
  Adder #(.width(32)) adder_1 (.a(SrcA), .b(SrcB), .out(adder_1_out));  // open: cin, cout
  Shifter #(.width(32)) shifter_1 (.in(SrcB), .\dist (s), .out(shifter_1_out));
  assign and_2_out = SrcA & ~SrcB;  // AND_Gate and_2, 32 bits wide
  assign or_2_out = SrcA | ~SrcB;  // OR_Gate or_2, 32 bits wide
  Subtractor #(.width(32)) subtractor_1 (.a(SrcA), .b(SrcB), .out(subtractor_1_out));  // open: bin, bout
  Shifter #(.width(32)) shifter_2 (.in(SrcB), .\dist (5'b10000), .out(shifter_2_out));
  Multiplexer #(.select(3), .width(32), .enable("false")) multiplexer_1 (
    .in0(and_1_out), .in1(or_1_out), .in2(adder_1_out), .in3(shifter_1_out), .in4(and_2_out), .in5(or_2_out),
    .in6(subtractor_1_out), .in7(shifter_2_out), .out(ALUResult), .sel(ALUop));
  Comparator #(.width(32), .mode("unsigned")) comparator_1 (.a({32{1'b0}}), .b(ALUResult), .eq(Zero));  // open: gt, lt
endmodule

// Controller
module controller (
  input  [5:0] OP,
  input  [5:0] Funct,
  output MemtoReg,
  output MemWrite,
  output Branch,
  output [2:0] ALUop_2_0,
  output ALUSrc,
  output RegDst,
  output RegWrite,
  output ExtOp
);

  wire addu, beq, lui, lw, ori, sll, subu, sw;

  and u_addu (addu, ~OP[5], ~OP[4], ~OP[3], ~OP[2], ~OP[1], ~OP[0], Funct[5], ~Funct[4], ~Funct[3], ~Funct[2], ~Funct[1], Funct[0]);  // AND_Gate
  and u_ori (ori, ~OP[5], ~OP[4], OP[3], OP[2], ~OP[1], OP[0]);  // AND_Gate
  and u_sw (sw, OP[5], ~OP[4], OP[3], ~OP[2], OP[1], OP[0]);  // AND_Gate
  and u_lui (lui, ~OP[5], ~OP[4], OP[3], OP[2], OP[1], OP[0]);  // AND_Gate
  and u_subu (subu, ~OP[5], ~OP[4], ~OP[3], ~OP[2], ~OP[1], ~OP[0], Funct[5], ~Funct[4], ~Funct[3], ~Funct[2], Funct[1], Funct[0]);  // AND_Gate
  and u_lw (lw, OP[5], ~OP[4], ~OP[3], ~OP[2], OP[1], OP[0]);  // AND_Gate
  and u_beq (beq, ~OP[5], ~OP[4], ~OP[3], OP[2], ~OP[1], ~OP[0]);  // AND_Gate
  and addu_2 (sll, ~OP[5], ~OP[4], ~OP[3], ~OP[2], ~OP[1], ~OP[0], ~Funct[5], ~Funct[4], ~Funct[3], ~Funct[2], ~Funct[1], ~Funct[0]);  // AND_Gate
  or u_RegWrite (RegWrite, addu, subu, ori, lw, lui, sll);
  or u_RegDst (RegDst, addu, subu, sll);
  or u_ALUSrc (ALUSrc, ori, lw, lui, sw);
  buf u_Branch (Branch, beq);  // OR_Gate
  buf u_ExtOp (ExtOp, ori);  // OR_Gate
  buf u_MemWrite (MemWrite, sw);  // OR_Gate
  buf u_MemtoReg (MemtoReg, lw);  // OR_Gate
  or ALUOp_2 (ALUop_2_0[2], subu, lui, beq);
  or ALUOp_1 (ALUop_2_0[1], subu, lui, beq, addu, lw, sw, sll);
  or ALUOp_0 (ALUop_2_0[0], ori, lui, sll);

  // Other names for the same wires on the sheet: ALUOp_0 = ALUop_2_0[0]; ALUOp_1 = ALUop_2_0[1];
  //   ALUOp_2 = ALUop_2_0[2]
endmodule

module InsSplitter (
  input  [31:0] instructure,
  output [5:0] Op,
  output [5:0] Funct,
  output [4:0] rs,
  output [4:0] rt,
  output [4:0] rd,
  output [4:0] s,
  output [15:0] imme
);


  assign Funct = instructure[5:0];
  assign imme = instructure[15:0];
  assign Op = instructure[31:26];
  assign rd = instructure[15:11];
  assign rs = instructure[25:21];
  assign rt = instructure[20:16];
  assign s = instructure[10:6];

  // Other names for the same wires on the sheet: _0 = instructure[0]; _1 = instructure[1]; _2 = instructure[2];
  //   _3 = instructure[3]; _4 = instructure[4]; _5 = instructure[5]; _6 = instructure[6]; _7 = instructure[7];
  //   _8 = instructure[8]; _9 = instructure[9]; _10 = instructure[10]; _11 = instructure[11]; _12 = instructure[12];
  //   _13 = instructure[13]; _14 = instructure[14]; _15 = instructure[15]; _26 = instructure[26];
  //   _27 = instructure[27]; _28 = instructure[28]; _29 = instructure[29]; _30 = instructure[30];
  //   _31 = instructure[31]; _21 = instructure[21]; _22 = instructure[22]; _23 = instructure[23];
  //   _24 = instructure[24]; _25 = instructure[25]; _16 = instructure[16]; _17 = instructure[17];
  //   _18 = instructure[18]; _19 = instructure[19]; _20 = instructure[20]
endmodule

// EXT
module ext (
  input  [15:0] In,
  input  ExtOp,
  output [31:0] Out
);

  wire [31:0] bit_extender_1_out, bit_extender_2_out;

  assign bit_extender_1_out = {{16{In[15]}}, In};  // Bit_Extender bit_extender_1
  assign bit_extender_2_out = {{16{1'b0}}, In};  // Bit_Extender bit_extender_2
  Multiplexer #(.width(32), .enable("false")) multiplexer_1 (
    .in0(bit_extender_1_out), .in1(bit_extender_2_out), .out(Out), .sel(ExtOp));
endmodule
